// Logisim project alu.circ as structural Verilog: 7 circuits, main circuit main
module main (
  input  [15:0] X,
  input  [15:0] Y,
  input  [3:0] switch__S,
  output signed_overflow,
  output [15:0] result,
  output equal
);

  wire addOverflow, addp8Overflow, divp8Overflow, mulp8Overflow, subOverflow, subp8Overflow;
  wire [0:0] sltOut;
  wire [15:0] addOut, addp8Out, andOut, divp8Out, mulp8Out, orOut, sllOut, sraOut, srlOut, subOut, subp8Out;

  Comparator #(.width(16)) comparator_1 (.a(X), .b(Y), .eq(equal));  // open: gt, lt
  Add add (.in_1(X), .in_2(Y), .out_3(addOut), .out_4(addOverflow));
  sub sub (.in_1(X), .in_2(Y), .out_3(subOut), .out_4(subOverflow));
  Shifter #(.width(16)) shifter_1 (.in(X), .\dist (Y[3:0]), .out(sllOut));
  Shifter #(.width(16), .shift("lr")) shifter_2 (.in(X), .\dist (Y[3:0]), .out(srlOut));
  Shifter #(.width(16), .shift("ar")) shifter_3 (.in(X), .\dist (Y[3:0]), .out(sraOut));
  Comparator #(.width(16)) comparator_2 (.a(X), .b(Y), .lt(sltOut[0]));  // open: gt, eq
  assign orOut = X | Y;  // OR_Gate or_1, 16 bits wide
  assign andOut = X & Y;  // AND_Gate and_1, 16 bits wide
  mulp8 mulp8 (.in_1(X), .in_2(Y), .out_3(mulp8Out), .out(mulp8Overflow));
  divp8 divp8 (.in_1(X), .in_2(Y), .out_3(divp8Out), .out(divp8Overflow));
  addp8 addp8 (.in_1(X), .in_2(Y), .out_3(addp8Out), .out_4(addp8Overflow));
  subp8 subp8_1 (.in_1(X), .in_2(Y), .out_3(subp8Out), .out_4(subp8Overflow));
  Multiplexer #(.select(4), .width(16)) multiplexer_1 (
    .in0(addOut), .in1(subOut), .in2(sllOut), .in3(srlOut), .in4(sraOut), .in5({{15{1'b0}}, sltOut[0]}),
    .in6(orOut), .in7(andOut), .in8(mulp8Out), .in9(divp8Out), .in10(addp8Out), .in11(subp8Out),
    .out(result), .sel(switch__S));  // open: in12, in13, in14, in15, en
  Multiplexer #(.select(4)) multiplexer_2 (
    .in0(addOverflow), .in1(subOverflow), .in2(1'b0), .in3(1'b0), .in4(1'b0), .in5(1'b0), .in6(1'b0),
    .in7(1'b0), .in8(mulp8Overflow), .in9(divp8Overflow), .in10(addp8Overflow), .in11(subp8Overflow),
    .in12(1'b0), .in13(1'b0), .in14(1'b0), .in15(1'b0), .out(signed_overflow), .sel(switch__S));  // open: en

  // Other names for the same wires on the sheet: overflow = signed_overflow; selector[3:0] = switch__S

  // Notes on the sheet:
  //   These are INPUTS to your circuit
  //   This is an INPUT to your circuit
  //   These are OUTPUTS to your circuit
endmodule

module Add (
  input  [15:0] in_1,
  input  [15:0] in_2,
  output [15:0] out_3,
  output out_4
);

  wire xor_1_out, xor_2_out;

  Adder #(.width(16)) adder_1 (.a(in_1), .b(in_2), .out(out_3));  // open: cin, cout
  xor xor_1 (xor_1_out, out_3[15], in_2[15]);
  xor xor_2 (xor_2_out, out_3[15], in_1[15]);
  and and_1 (out_4, xor_1_out, xor_2_out);
endmodule

module sub (
  input  [15:0] in_1,
  input  [15:0] in_2,
  output [15:0] out_3,
  output out_4
);

  wire comparator_1_eq, comparator_2_eq, not_1_out;

  Comparator #(.width(1)) comparator_1 (.a(in_2[15]), .b(in_1[15]), .eq(comparator_1_eq));  // open: gt, lt
  Subtractor #(.width(16)) subtractor_1 (.a(in_1), .b(in_2), .out(out_3));  // open: bin, bout
  Comparator #(.width(1)) comparator_2 (.a(out_3[15]), .b(in_2[15]), .eq(comparator_2_eq));  // open: gt, lt
  not not_1 (not_1_out, comparator_1_eq);
  and and_1 (out_4, comparator_2_eq, not_1_out);
endmodule

module mulp8 (
  input  [15:0] in_1,
  input  [15:0] in_2,
  output [15:0] out_3,
  output out
);

  wire xor_1_out, xor_2_out;

  Multiplier multiplier_1 (.a(in_1[7:0]), .b(in_2[7:0]), .out(out_3[7:0]));  // open: cin, cout
  Multiplier multiplier_2 (.a(in_1[15:8]), .b(in_2[15:8]), .out(out_3[15:8]));  // open: cin, cout
  xor xor_1 (xor_1_out, out_3[15], in_1[15]);
  xor xor_2 (xor_2_out, out_3[15], in_2[15]);
  and and_1 (out, xor_1_out, xor_2_out);
endmodule

module divp8 (
  input  [15:0] in_1,
  input  [15:0] in_2,
  output [15:0] out_3,
  output out
);

  wire xor_1_out, xor_2_out;

  Divider divider_1 (.a(in_1[7:0]), .b(in_2[7:0]), .out(out_3[7:0]));  // open: upper, rem
  Divider divider_2 (.a(in_1[15:8]), .b(in_2[15:8]), .out(out_3[15:8]));  // open: upper, rem
  xor xor_1 (xor_1_out, out_3[15], in_1[15]);
  xor xor_2 (xor_2_out, out_3[15], in_2[15]);
  and and_1 (out, xor_1_out, xor_2_out);
endmodule

module addp8 (
  input  [15:0] in_1,
  input  [15:0] in_2,
  output [15:0] out_3,
  output out_4
);

  wire and_1_out, and_2_out, comparator_1_eq, comparator_2_eq, not_1_out, not_2_out;

  Adder adder_1 (.a(in_1[7:0]), .b(in_2[7:0]), .out(out_3[7:0]));  // open: cin, cout
  Adder adder_2 (.a(in_1[15:8]), .b(in_2[15:8]), .out(out_3[15:8]));  // open: cin, cout
  and and_1 (and_1_out, in_1[7], in_2[7]);
  and and_2 (and_2_out, in_2[15], in_1[15]);
  not not_1 (not_1_out, out_3[15]);
  Comparator #(.width(1), .mode("unsigned")) comparator_1 (
    .a(not_1_out), .b(and_2_out), .eq(comparator_1_eq));  // open: gt, lt
  not not_2 (not_2_out, out_3[7]);
  Comparator #(.width(1), .mode("unsigned")) comparator_2 (
    .a(not_2_out), .b(and_1_out), .eq(comparator_2_eq));  // open: gt, lt
  or or_1 (out_4, comparator_2_eq, comparator_1_eq);
endmodule

module subp8 (
  input  [15:0] in_1,
  input  [15:0] in_2,
  output [15:0] out_3,
  output out_4
);

  wire and_1_out, and_2_out, comparator_1_eq, comparator_2_eq, comparator_3_eq, comparator_4_eq, not_1_out,
       not_2_out;

  Subtractor subtractor_1 (.a(in_1[7:0]), .b(in_2[7:0]), .out(out_3[7:0]));  // open: bin, bout
  Subtractor subtractor_2 (.a(in_1[15:8]), .b(in_2[15:8]), .out(out_3[15:8]));  // open: bin, bout
  Comparator #(.width(1)) comparator_1 (.a(in_1[7]), .b(in_2[7]), .eq(comparator_1_eq));  // open: gt, lt
  Comparator #(.width(1)) comparator_2 (.a(in_1[15]), .b(in_2[15]), .eq(comparator_2_eq));  // open: gt, lt
  not not_1 (not_1_out, comparator_2_eq);
  Comparator #(.width(1)) comparator_3 (.a(out_3[7]), .b(in_2[7]), .eq(comparator_3_eq));  // open: gt, lt
  not not_2 (not_2_out, comparator_1_eq);
  Comparator #(.width(1)) comparator_4 (.a(out_3[15]), .b(in_2[15]), .eq(comparator_4_eq));  // open: gt, lt
  and and_1 (and_1_out, comparator_3_eq, not_2_out);
  and and_2 (and_2_out, comparator_4_eq, not_1_out);
  or or_1 (out_4, and_1_out, and_2_out);
endmodule
