// Logisim project Regfile.circ as structural Verilog: 1 circuit, main circuit main
module main (
  input  [1:0] Read_register_1,
  input  [1:0] Read_register_2,
  input  [1:0] write_register,
  input  [15:0] write_data,
  input  RegWrite,
  input  clock,
  output [15:0] Reg_0_Value,
  output [15:0] Reg_1_Value,
  output [15:0] Reg_2_Value,
  output [15:0] Reg_3_Value,
  output [15:0] Read_Data_1,
  output [15:0] Read_Data_2
);

  wire [15:0] multiplexer_1_out, multiplexer_2_out, multiplexer_3_out, multiplexer_4_out;

  Multiplexer #(.select(2), .width(16)) multiplexer_1 (
    .in0(write_data), .out(multiplexer_1_out), .sel(write_register), .en(RegWrite));  // open: in1, in2, in3
  Register #(.width(16)) Reg_0 (.D(multiplexer_1_out), .Q(Reg_0_Value), .clk(clock));  // open: en, clr
  Multiplexer #(.select(2), .width(16)) multiplexer_2 (
    .in1(write_data), .out(multiplexer_2_out), .sel(write_register), .en(RegWrite));  // open: in0, in2, in3
  Register #(.width(16)) Reg_1 (.D(multiplexer_2_out), .Q(Reg_1_Value), .clk(clock));  // open: en, clr
  Register #(.width(16)) Reg_2 (.D(multiplexer_3_out), .Q(Reg_2_Value), .clk(clock));  // open: en, clr
  Multiplexer #(.select(2), .width(16)) multiplexer_3 (
    .in2(write_data), .out(multiplexer_3_out), .sel(write_register), .en(RegWrite));  // open: in0, in1, in3
  Multiplexer #(.select(2), .width(16)) multiplexer_4 (
    .in3(write_data), .out(multiplexer_4_out), .sel(write_register), .en(RegWrite));  // open: in0, in1, in2
  Register #(.width(16)) Reg_3 (.D(multiplexer_4_out), .Q(Reg_3_Value), .clk(clock));  // open: en, clr
  Multiplexer #(.select(2), .width(16)) multiplexer_5 (
    .in0(Reg_0_Value), .in1(Reg_1_Value), .in2(Reg_2_Value), .in3(Reg_3_Value), .out(Read_Data_2),
    .sel(Read_register_2));  // open: en
  Multiplexer #(.select(2), .width(16)) multiplexer_6 (
    .in0(Reg_0_Value), .in1(Reg_1_Value), .in2(Reg_2_Value), .in3(Reg_3_Value), .out(Read_Data_1),
    .sel(Read_register_1));  // open: en

  // Other names for the same wires on the sheet: clk = clock; Read_Reg_1[1:0] = Read_register_1;
  //   Read_Reg_2[1:0] = Read_register_2; Reg0[15:0] = Reg_0_Value; Reg1[15:0] = Reg_1_Value; Reg2[15:0] = Reg_2_Value;
  //   Reg3[15:0] = Reg_3_Value

  // Notes on the sheet:
  //   These are INPUTS to the circuit
  //   These are INPUTS to the circuit
  //   DO NOT CHANGE THE LOCATIONS OF THE INPUTS/OUTPUTS! IF YOU DO SO, YOU NEED TO MAKE SURE THE PINS ARE AT THE RIGHT PLACE!
  //   These are OUTPUTS to the circuit
  //   Yet again, the clock is not an actual clock, but an input, one that will be driven from a higher circuit
  //   These are OUTPUTS to the circuit
endmodule
