// Logisim project cpu.circ as structural Verilog: 2 circuits, main circuit main
// CPU
module main (
  input  [15:0] From_Instr_Mem,
  input  clk,
  output [15:0] r0,
  output [15:0] r1,
  output [15:0] r2,
  output [15:0] r3,
  output [15:0] Display_0,
  output [15:0] Display_1,
  output [15:0] To_Instr_Mem,
  output [15:0] Data_Mem_Data,
  output [15:0] Data_Mem_Addr,
  output Data_Mem_Write
);

  wire aluSrc, and_1_out, and_3_out, and_4_out, and_5_out, button_1_out, comparator_1_eq, comparator_2_eq,
       disp, equal, jal, lui, memtoReg, multiplexer_12_out, multiplexer_17_out, multiplexer_21_out, nop,
       not_1_out, not_2_out, overFlow, rt_rd, rW, sign, undriven, undriven_2;
  wire [1:0] multiplexer_1_out, multiplexer_2_out;
  wire [3:0] ALU_control_out_3;
  wire [15:0] adder_1_out, adder_3_out, adder_4_out, adder_5_out, adder_6_out, adder_7_out, adder_8_out,
       ALU_result, and_2_out, beq, bit_extender_1_out, bit_extender_2_out, bit_extender_3_out, bne, imm,
       instrInput, multiplexer_3_out, multiplexer_4_out, multiplexer_7_out, multiplexer_9_out,
       multiplexer_10_out, multiplexer_23_out, multiplexer_26_out, nextPC, or_2_out, regWrite_read_data_2,
       rs, writeData;

  Multiplexer #(.width(2)) multiplexer_1 (
    .in0(2'b11), .in1(multiplexer_2_out), .out(multiplexer_1_out), .sel(jal));  // open: en
  Multiplexer #(.width(2)) multiplexer_2 (
    .in0(instrInput[9:8]), .in1(instrInput[7:6]), .out(multiplexer_2_out), .sel(rt_rd));  // open: en
  Multiplexer #(.width(16)) multiplexer_3 (
    .in0(To_Instr_Mem), .in1(writeData), .out(multiplexer_3_out), .sel(jal));  // open: en
  assign bit_extender_1_out = {{8{1'b0}}, instrInput[7:0]};  // Bit_Extender bit_extender_1
  // Probe on 16'h50fe
  Multiplexer #(.width(16)) multiplexer_4 (
    .in0(From_Instr_Mem), .in1(16'h6), .out(multiplexer_4_out), .sel(nop));  // open: en
  Multiplexer #(.select(4)) multiplexer_5 (
    .in0(1'b0), .in1(1'b0), .in2(1'b0), .in3(1'b0), .in4(1'b0), .in5(1'b1), .in6(1'b1), .in7(1'b1),
    .in8(1'b0), .in9(1'b1), .in10(1'b1), .in11(1'b1), .in12(1'b1), .in13(1'b0), .in14(1'b0), .in15(1'b0),
    .out(aluSrc), .sel(instrInput[15:12]));  // open: en
  Multiplexer #(.select(4)) multiplexer_6 (
    .in0(1'b1), .in1(1'b1), .in2(1'b1), .in3(1'b1), .in4(1'b1), .in5(1'b1), .in6(1'b1), .in7(1'b1),
    .in8(1'b1), .in9(1'b1), .in10(1'b1), .in11(1'b0), .in12(1'b1), .in13(1'b1), .in14(1'b1), .in15(1'b1),
    .out(memtoReg), .sel(instrInput[15:12]));  // open: en
  Regfile_main regWrite (
    .Read_register_1(instrInput[11:10]), .Read_register_2(instrInput[9:8]),
    .write_register(multiplexer_1_out), .write_data(multiplexer_3_out), .Reg_0_Value(r0), .Reg_1_Value(r1),
    .Reg_2_Value(r2), .Reg_3_Value(r3), .RegWrite(rW), .clock(clk), .Read_Data_1(rs),
    .Read_Data_2(regWrite_read_data_2));
  Multiplexer #(.width(16)) multiplexer_7 (
    .in0(regWrite_read_data_2), .in1(imm), .out(multiplexer_7_out), .sel(aluSrc));  // open: en
  assign bit_extender_2_out = {{8{instrInput[7]}}, instrInput[7:0]};  // Bit_Extender bit_extender_2
  Multiplexer #(.width(16)) multiplexer_8 (
    .in0(bit_extender_2_out), .in1(bit_extender_1_out), .out(imm), .sel(sign));  // open: en
  Register #(.width(16)) register_1 (.D(multiplexer_4_out), .Q(instrInput), .clk(clk));  // open: en, clr
  Multiplexer #(.width(16)) multiplexer_9 (.in0(rs), .in1(imm), .out(multiplexer_9_out), .sel(lui));  // open: en
  Multiplexer #(.width(16)) multiplexer_10 (
    .in0(multiplexer_7_out), .in1(16'h8), .out(multiplexer_10_out), .sel(lui));  // open: en
  aluControl ALU_control (.funct(instrInput[3:0]), .opCode(instrInput[15:12]), .out_3(ALU_control_out_3));
  // Probe on 16'h75ad
  alu_main ALU (
    .switch__S(ALU_control_out_3), .X(multiplexer_9_out), .equal(equal), .result(ALU_result),
    .signed_overflow(overFlow), .Y(multiplexer_10_out));
  // Probe on 16'ha1de
  Multiplexer #(.select(4)) multiplexer_11 (
    .in0(1'b0), .in1(1'b0), .in2(1'b0), .in3(1'b0), .in4(1'b0), .in5(1'b0), .in6(1'b0), .in7(1'b0),
    .in8(1'b0), .in9(1'b1), .in10(1'b0), .in11(1'b0), .in12(1'b0), .in13(1'b0), .in14(1'b0), .in15(1'b0),
    .out(Data_Mem_Write), .sel(instrInput[15:12]));  // open: en
  Multiplexer #(.select(4)) multiplexer_12 (
    .in0(1'b0), .in1(1'b1), .in2(1'b1), .in3(1'b1), .in4(1'b0), .in5(1'b0), .in6(1'b0), .in7(1'b0),
    .in8(1'b0), .in9(1'b0), .in10(1'b0), .in11(1'b0), .in12(1'b0), .in13(1'b0), .in14(1'b0), .in15(1'b0),
    .out(multiplexer_12_out), .sel(instrInput[15:12]));  // open: en
  Multiplexer #(.select(4)) multiplexer_13 (
    .in0(1'b1), .in1(1'b0), .in2(1'b1), .in3(1'b1), .in4(1'b1), .in5(1'b1), .in6(1'b1), .in7(1'b1),
    .in8(1'b1), .in9(1'b1), .in10(1'b1), .in11(1'b1), .in12(1'b1), .in13(1'b1), .in14(1'b1), .in15(1'b1),
    .out(jal), .sel(instrInput[15:12]), .en(undriven));
  assign Data_Mem_Data = Data_Mem_Write ? regWrite_read_data_2 : 16'bz;  // Controlled_Buffer controlled_buffer_1
  not not_1 (not_1_out, Data_Mem_Write);
  Multiplexer #(.select(4)) multiplexer_14 (
    .in0(1'b0), .in1(1'b0), .in2(1'b0), .in3(1'b0), .in4(1'b0), .in5(1'b0), .in6(1'b0), .in7(1'b0),
    .in8(1'b0), .in9(1'b0), .in10(1'b0), .in11(1'b0), .in12(1'b1), .in13(1'b0), .in14(1'b0), .in15(1'b0),
    .out(disp), .sel(instrInput[15:12]), .en(undriven_2));
  or or_1 (nop, multiplexer_12_out, and_1_out, and_3_out);
  LED u_overFlow (.in(overFlow));
  RAM #(.addrWidth(16), .dataWidth(16)) ram_1 (
    .addr(ALU_result), .data(Data_Mem_Data), .sel(1'b1), .clk(clk), .ld(not_1_out), .clr(button_1_out));
  Multiplexer #(.width(16)) multiplexer_15 (
    .in0(Data_Mem_Data), .in1(ALU_result), .out(writeData), .sel(memtoReg));  // open: en
  Button button_1 (.out(button_1_out));
  Multiplexer #(.select(4)) multiplexer_16 (
    .in0(1'b1), .in1(1'b1), .in2(1'b0), .in3(1'b0), .in4(1'b0), .in5(1'b1), .in6(1'b1), .in7(1'b1),
    .in8(1'b0), .in9(1'b0), .in10(1'b1), .in11(1'b1), .in12(1'b0), .in13(1'b0), .in14(1'b0), .in15(1'b0),
    .out(rW), .sel(instrInput[15:12]));  // open: en
  Multiplexer #(.select(4)) multiplexer_17 (
    .in0(1'b0), .in1(1'b0), .in2(1'b0), .in3(1'b0), .in4(1'b1), .in5(1'b0), .in6(1'b0), .in7(1'b0),
    .in8(1'b0), .in9(1'b0), .in10(1'b0), .in11(1'b0), .in12(1'b0), .in13(1'b0), .in14(1'b0), .in15(1'b0),
    .out(multiplexer_17_out), .sel(instrInput[15:12]));  // open: en
  Register #(.width(16)) register_2 (.D(nextPC), .Q(To_Instr_Mem), .clk(clk));  // open: en, clr
  Multiplexer #(.select(4)) multiplexer_18 (
    .in0(1'b1), .in1(1'b0), .in2(1'b0), .in3(1'b0), .in4(1'b0), .in5(1'b0), .in6(1'b0), .in7(1'b0),
    .in8(1'b0), .in9(1'b0), .in10(1'b0), .in11(1'b0), .in12(1'b0), .in13(1'b0), .in14(1'b0), .in15(1'b0),
    .out(rt_rd), .sel(instrInput[15:12]));  // open: en
  and and_1 (and_1_out, multiplexer_17_out, equal);
  assign and_2_out = To_Instr_Mem & 16'hf000;  // AND_Gate and_2, 16 bits wide
  assign bit_extender_3_out = {{4{1'b0}}, instrInput[11:0]};  // Bit_Extender bit_extender_3
  Adder #(.width(16)) adder_1 (.a(To_Instr_Mem), .b(16'h1), .out(adder_1_out));  // open: cin, cout
  assign or_2_out = and_2_out | bit_extender_3_out;  // OR_Gate or_2, 16 bits wide
  Adder #(.width(16)) adder_2 (.a(rs), .b(imm), .out(Data_Mem_Addr));  // open: cin, cout
  Hex_Digit_Display hex_digit_display_1 (.value(Display_0[15:12]));  // open: dp
  Multiplexer #(.select(4), .width(16)) multiplexer_19 (
    .in0(adder_1_out), .in1(or_2_out), .in2(or_2_out), .in3(rs), .in4(beq), .in5(adder_1_out),
    .in6(adder_1_out), .in7(adder_1_out), .in8(bne), .in9(adder_1_out), .in10(adder_1_out),
    .in11(adder_1_out), .in12(adder_1_out), .out(nextPC), .sel(instrInput[15:12]));  // open: in13, in14, in15, en
  Multiplexer #(.select(4)) multiplexer_20 (
    .in0(1'b0), .in1(1'b0), .in2(1'b0), .in3(1'b0), .in4(1'b0), .in5(1'b0), .in6(1'b0), .in7(1'b0),
    .in8(1'b0), .in9(1'b0), .in10(1'b1), .in11(1'b0), .in12(1'b0), .in13(1'b0), .in14(1'b0), .in15(1'b0),
    .out(lui), .sel(instrInput[15:12]));  // open: en
  Multiplexer #(.select(4)) multiplexer_21 (
    .in0(1'b0), .in1(1'b0), .in2(1'b0), .in3(1'b0), .in4(1'b0), .in5(1'b0), .in6(1'b0), .in7(1'b0),
    .in8(1'b1), .in9(1'b0), .in10(1'b0), .in11(1'b0), .in12(1'b0), .in13(1'b0), .in14(1'b0), .in15(1'b0),
    .out(multiplexer_21_out), .sel(instrInput[15:12]));  // open: en
  Hex_Digit_Display hex_digit_display_2 (.value(Display_0[7:4]));  // open: dp
  Hex_Digit_Display hex_digit_display_3 (.value(Display_0[11:8]));  // open: dp
  and and_3 (and_3_out, multiplexer_21_out, not_2_out);
  not not_2 (not_2_out, equal);
  Hex_Digit_Display hex_digit_display_4 (.value(Display_0[3:0]));  // open: dp
  Comparator #(.width(1)) comparator_1 (.a(imm[0]), .b(1'b0), .eq(comparator_1_eq));  // open: gt, lt
  and and_4 (and_4_out, comparator_1_eq, disp);
  Adder #(.width(16)) adder_3 (.a(To_Instr_Mem), .b({16{1'b0}}), .out(adder_3_out));  // open: cin, cout
  Adder #(.width(16)) adder_4 (.a(To_Instr_Mem), .b({16{1'b0}}), .out(adder_4_out));  // open: cin, cout
  Multiplexer #(.select(4)) multiplexer_22 (
    .in0(1'b0), .in1(1'b0), .in2(1'b0), .in3(1'b0), .in4(1'b0), .in5(1'b0), .in6(1'b1), .in7(1'b1),
    .in8(1'b0), .in9(1'b0), .in10(1'b1), .in11(1'b0), .in12(1'b1), .in13(1'b0), .in14(1'b0), .in15(1'b0),
    .out(sign), .sel(instrInput[15:12]));  // open: en
  Hex_Digit_Display hex_digit_display_5 (.value(Display_1[11:8]));  // open: dp
  Hex_Digit_Display hex_digit_display_6 (.value(Display_1[15:12]));  // open: dp
  Register #(.width(16)) register_3 (.D(multiplexer_23_out), .Q(Display_0), .clk(clk));  // open: en, clr
  Multiplexer #(.width(16)) multiplexer_23 (
    .in0(Display_0), .in1(rs), .out(multiplexer_23_out), .sel(and_4_out));  // open: en
  Adder #(.width(16)) adder_5 (.a(To_Instr_Mem), .b(16'h1), .out(adder_5_out));  // open: cin, cout
  Adder #(.width(16)) adder_6 (.a(adder_3_out), .b(imm), .out(adder_6_out));  // open: cin, cout
  Adder #(.width(16)) adder_7 (.a(adder_4_out), .b(imm), .out(adder_7_out));  // open: cin, cout
  Adder #(.width(16)) adder_8 (.a(To_Instr_Mem), .b(16'h1), .out(adder_8_out));  // open: cin, cout
  Hex_Digit_Display hex_digit_display_7 (.value(Display_1[7:4]));  // open: dp
  Hex_Digit_Display hex_digit_display_8 (.value(Display_1[3:0]));  // open: dp
  Multiplexer #(.width(16)) multiplexer_24 (.in0(adder_5_out), .in1(adder_6_out), .out(beq), .sel(equal));  // open: en
  Multiplexer #(.width(16)) multiplexer_25 (.in0(adder_7_out), .in1(adder_8_out), .out(bne), .sel(equal));  // open: en
  // Probe on multiplexer_26_out
  Comparator #(.width(1)) comparator_2 (.a(imm[0]), .b(1'b1), .eq(comparator_2_eq));  // open: gt, lt
  and and_5 (and_5_out, comparator_2_eq, disp);
  Register #(.width(16)) register_4 (.D(multiplexer_26_out), .Q(Display_1), .clk(clk));  // open: en, clr
  Multiplexer #(.width(16)) multiplexer_26 (
    .in0(Display_1), .in1(rs), .out(multiplexer_26_out), .sel(and_5_out));  // open: en

  // Other names for the same wires on the sheet: clock = clk; d0[15:0] = Display_0; d1[15:0] = Display_1;
  //   target[11:0] = instrInput[11:0]; opCode[3:0] = instrInput[15:12]; memWrite = Data_Mem_Write;
  //   PC[15:0] = To_Instr_Mem

  // Notes on the sheet:
  //   rs
  //   rt
  //   rd
  //   funct
  //   This is the current PC that you need to send as OUTPUT
  //   This is the instruction that you would receive as INPUT
  //   This is a CLK that is an INPUT driven from the harness.
  //   Remember, this circuit is loaded from the harness to be tested!
  //   These are OUTPUTS to the circuit
  //   PC + 1
  //   jump
  //   These are OUTPUTS to the circuit
  //   Branch if Equal
  //   Branch
  //   Branch not Equal
  //   Branch
endmodule

module aluControl (
  input  [3:0] funct,
  input  [3:0] opCode,
  output [3:0] out_3
);

  Multiplexer #(.select(4), .width(4)) multiplexer_1 (
    .in0(funct), .in1(funct), .in2(funct), .in3(funct), .in4(funct), .in5(4'b0000), .in6(4'b0111),
    .in7(4'b0110), .in8(funct), .in9(4'b0000), .in10(4'b0010), .in11(4'b0000), .in12(funct), .in13(funct),
    .in14(funct), .in15(funct), .out(out_3), .sel(opCode));  // open: en
endmodule
